# Fritzing sketch skps (saved by Fritzing 0.9.3b)
breadboards: 1

parts:
  Mod1 = Raspberry Pi 4B
  R1 = Resistor [tolerance=±5% resistance=4.7k package=THT]
  R2 = Resistor [tolerance=±5% resistance=4.7k package=THT]
  J1 = Basic Servo
  Part1 = Adafruit VL530X Time of Flight Distance Sensor [part_number="Adafruit #3317"]

nets:
  3V3: Mod1.3V3, Part1.VCC
  N1: Mod1.GPIO2, R2.Pin_1
  5V: Mod1.5V, J1.vcc
  N2: Mod1.GPIO3, R1.Pin_0
  GND: Mod1.GND, J1.gnd, Part1.GND
  N3: Mod1.GPIO4, J1.pulse
  N4: R1.Pin_1, Part1.SCL

custom parts:
  Adafruit VL530X Time of Flight Distance Sensor: The VL53L0X is a Time of Flight distance sensor like no other you've used! The sensor contains a very tiny invisible laser source, and a matching sensor. The VL53L0X can detect the "time of flight", or how long the light has taken to bounce back to the sensor. Since it uses a very narrow light source, it is good for determining distance of only the surface directly in front of it. Unlike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
